# Fritzing sketch safebox_keypad_multipassword (saved by Fritzing 0.9.2b)
breadboards: 1

parts:
  Part1 = Arduino Uno (Rev3)
  PCB2 = RTC_DS1302_module
  KY-1 = Keyes Relay [package=THT]
  J1 = Piezo Speaker
  Display1 = LCD screen 16x2 IIC [part_number=101290]
  Matrix_keypad1 = KEYPAD 4x4
  SD_card_module1 = SD Card Module
  R2 = Resistor [tolerance=±5% resistance=220 package="0402 [SMD]"]
  M1 = DC Motor
  VCC1 = 4 x AAA Battery Mount

nets:
  N1: Part1.A0, KY-1.signal
  N2: Part1.A1, PCB2.CLK
  N3: Part1.A2, PCB2.DAT
  N4: Part1.A3, PCB2.RST
  N5: Part1.D8, J1.pin2
  N6: Part1.D10_PWM/SS, SD_card_module1.CS
  N7: Part1.D11_PWM/MOSI, SD_card_module1.MOSI
  N8: Part1.D12/MISO, SD_card_module1.MISO
  N9: Part1.D13/SCK, SD_card_module1.SCK
  GND: Part1.GND, PCB2.GND, KY-1.ground, Display1.GND, R2.Pin_0
  N10: Part1.A4/SDA, Display1.SDA
  N11: Part1.A5/SCL, Display1.SCL
  N12: Part1.D0/RX, Matrix_keypad1.row4
  N13: Part1.D1/TX, Matrix_keypad1.row3
  N14: Part1.D2, Matrix_keypad1.row2
  N15: Part1.D3_PWM, Matrix_keypad1.row1
  N16: Part1.D4, Matrix_keypad1.col4
  N17: Part1.D5_PWM, Matrix_keypad1.col3
  N18: Part1.D6_PWM, Matrix_keypad1.col2
  N19: Part1.D7, Matrix_keypad1.col1
  VCC: Part1.5V, PCB2.VCC, KY-1.power, Display1.VCC, SD_card_module1.+5
  N20: KY-1.C, M1.pin_2
  N21: KY-1.NO, VCC1.-
  N22: J1.pin1, R2.Pin_1

custom parts:
  RTC_DS1302_module: Arduino module DS1302 SPI Real Time Clock
  Keyes Relay: The Keyes 5V relay module is suitable for SCM development, home appliance control. It uses a 5V~12V TIL control signal which can control DC / AC signal.
  LCD screen 16x2 IIC: LCD screen with HD44780 controller enables showing text, symbols, value or anything else that comes from Croduino/Arduino. It is capable of showing 16 symbols in two lines and therefore can be used in many projects that need to send clearly visible and legible output information.. • Color of symbols: White • Backlight: Blue • Dimensions: 80 x 36 x 12 mm • Screen dimensions: 64.5 x 16 mm •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
  KEYPAD 4x4: Matrix keypad 16 buttons, 4 rows x 4 columns
  SD Card Module: SD Card Module Slot Socket Reader For Arduino ARM MCU
